// Logisim project Assignment 2.circ as structural Verilog: 1 circuit, main circuit main
module main (
  input  As,
  input  Bs,
  input  M,
  input  [6:0] Result_A,
  input  [6:0] A,
  input  [6:0] B,
  input  [6:0] Final_A,
  input  [6:0] B_2,
  output signs,
  output Calling,
  output E,
  output Final_AS,
  output AVF
);

  wire comparator_1_eq, multiplexer_2_out, multiplexer_4_out, not_2_out;
  wire [6:0] adder_1_out, adder_2_out, multiplexer_1_out, multiplexer_3_out, multiplexer_5_out, not_1_out,
       not_3_out;

  assign not_1_out = ~B;  // NOT_Gate not_1, 7 bits wide
  xor xor_1 (signs, As, Bs);
  Multiplexer #(.width(7), .enable("false")) multiplexer_1 (
    .in0(B), .in1(not_1_out), .out(multiplexer_1_out), .sel(Calling));
  Comparator #(.width(7)) comparator_1 (.a(adder_1_out), .b(B_2), .eq(comparator_1_eq));  // open: gt, lt
  Adder #(.width(7)) adder_1 (.a(A), .b(multiplexer_1_out), .out(adder_1_out), .cin(Calling), .cout(E));
  Multiplexer #(.enable("false")) multiplexer_2 (.in0(As), .in1(1'b0), .out(multiplexer_2_out), .sel(comparator_1_eq));
  xor xor_2 (Calling, signs, M);
  not not_2 (not_2_out, As);
  assign not_3_out = ~adder_1_out;  // NOT_Gate not_3, 7 bits wide
  Multiplexer #(.width(7), .enable("false")) multiplexer_3 (
    .in0(adder_2_out), .in1(adder_1_out), .out(multiplexer_3_out), .sel(E));
  Multiplexer #(.enable("false")) multiplexer_4 (
    .in0(not_2_out), .in1(multiplexer_2_out), .out(multiplexer_4_out), .sel(E));
  Adder #(.width(7)) adder_2 (.a(not_3_out), .b(B_2), .out(adder_2_out));  // open: cin, cout
  Multiplexer #(.width(7), .enable("false")) multiplexer_5 (
    .in0(adder_1_out), .in1(multiplexer_3_out), .out(multiplexer_5_out), .sel(Calling));
  Multiplexer #(.enable("false")) multiplexer_6 (.in0(As), .in1(multiplexer_4_out), .out(Final_AS), .sel(Calling));
  Multiplexer #(.enable("false")) multiplexer_7 (.in0(E), .in1(1'b0), .out(AVF), .sel(Calling));

  // Notes on the sheet:
  //   Sign Bit of A
  //   Sign Bit of B
  //   Magnitude Part of number A
  //   Magnitude Part of number B
  //   23CS054
  //   Sign = 0 Both Numbers have same signs
  //   Sign = 1 Both Numbers have different signs
  //   M = 0 Addition
  //   M = 1 Subtraction
  //   Calling = 0 : Call Function 1
  //   Calling = 1: Call Function 2
  //   Function 1 Tasks: Add Magnitudes of both numbers and use the sign of A
  //   Function 2 Tasks: Subtract both numbers and use the sign of larger number
endmodule
