// Logisim project Assignment 3.circ as structural Verilog: 1 circuit, main circuit main
module main (
  input  [1:0] Select,
  input  [3:0] Input_for_Register_D,
  input  [3:0] Input_for_Register_C,
  input  [3:0] Input_for_Register_B,
  input  [3:0] Input_for_Register_A,
  input  in_6,
  output [3:0] out_7,
  output [3:0] out_8,
  output [3:0] out_9,
  output [3:0] out_10,
  output [3:0] out_11
);

  wire clock_1_out;

  Clock clock_1 (.out(clock_1_out));
  Multiplexer #(.select(2), .enable("false")) multiplexer_1 (
    .in0(out_11[3]), .in1(out_10[3]), .in2(out_9[3]), .in3(out_8[3]), .out(out_7[3]), .sel(Select));
  Register #(.width(4)) Register_D (.D(Input_for_Register_D), .en(1'b1), .Q(out_8), .clk(clock_1_out), .clr(in_6));
  Multiplexer #(.select(2), .enable("false")) multiplexer_2 (
    .in0(out_11[2]), .in1(out_10[2]), .in2(out_9[2]), .in3(out_8[2]), .out(out_7[2]), .sel(Select));
  Register #(.width(4)) Register_C (.D(Input_for_Register_C), .en(1'b1), .Q(out_9), .clk(clock_1_out), .clr(in_6));
  Multiplexer #(.select(2), .enable("false")) multiplexer_3 (
    .in0(out_11[1]), .in1(out_10[1]), .in2(out_9[1]), .in3(out_8[1]), .out(out_7[1]), .sel(Select));
  Register #(.width(4)) Register_B (.D(Input_for_Register_B), .en(1'b1), .Q(out_10), .clk(clock_1_out), .clr(in_6));
  Multiplexer #(.select(2), .enable("false")) multiplexer_4 (
    .in0(out_11[0]), .in1(out_10[0]), .in2(out_9[0]), .in3(out_8[0]), .out(out_7[0]), .sel(Select));
  Register #(.width(4)) Register_A (.D(Input_for_Register_A), .en(1'b1), .Q(out_11), .clk(clock_1_out), .clr(in_6));

  // Notes on the sheet:
  //   Select 00: A
  //   Select 01: B
  //   Select 10: C
  //   Select 11: D
  //   23CS054
endmodule
