// Logisim project Assignment 4.circ as structural Verilog: 1 circuit, main circuit main
module main (
  input  [1:0] Select,
  input  [3:0] Input_for_Register_D,
  input  [3:0] Input_for_Register_C,
  input  [3:0] Input_for_Register_B,
  input  [3:0] Input_for_Register_A,
  input  in_6,
  output [3:0] out_7,
  output [3:0] out_8,
  output [3:0] out_9,
  output [3:0] out_10,
  output [3:0] out_11
);

  wire clock_1_out, decoder_1_out0, decoder_1_out1, decoder_1_out2, decoder_1_out3;

  Clock clock_1 (.out(clock_1_out));
  Register #(.width(4)) Register_D (.D(Input_for_Register_D), .en(1'b1), .Q(out_8), .clk(clock_1_out), .clr(in_6));
  Decoder #(.select(2), .enable("false")) decoder_1 (
    .out0(decoder_1_out0), .out1(decoder_1_out1), .out2(decoder_1_out2), .out3(decoder_1_out3), .sel(Select));
  assign out_7[2] = decoder_1_out0 ? out_11[2] : 1'bz;  // Controlled_Buffer controlled_buffer_1
  assign out_7[3] = decoder_1_out0 ? out_11[3] : 1'bz;  // Controlled_Buffer controlled_buffer_2
  assign out_7[2] = decoder_1_out1 ? out_10[2] : 1'bz;  // Controlled_Buffer controlled_buffer_3
  assign out_7[3] = decoder_1_out1 ? out_10[3] : 1'bz;  // Controlled_Buffer controlled_buffer_4
  assign out_7[3] = decoder_1_out2 ? out_9[3] : 1'bz;  // Controlled_Buffer controlled_buffer_5
  assign out_7[2] = decoder_1_out2 ? out_9[2] : 1'bz;  // Controlled_Buffer controlled_buffer_6
  assign out_7[3] = decoder_1_out3 ? out_8[3] : 1'bz;  // Controlled_Buffer controlled_buffer_7
  assign out_7[2] = decoder_1_out3 ? out_8[2] : 1'bz;  // Controlled_Buffer controlled_buffer_8
  Register #(.width(4)) Register_C (.D(Input_for_Register_C), .en(1'b1), .Q(out_9), .clk(clock_1_out), .clr(in_6));
  assign out_7[1] = decoder_1_out0 ? out_11[1] : 1'bz;  // Controlled_Buffer controlled_buffer_9
  assign out_7[1] = decoder_1_out1 ? out_10[1] : 1'bz;  // Controlled_Buffer controlled_buffer_10
  assign out_7[1] = decoder_1_out2 ? out_9[1] : 1'bz;  // Controlled_Buffer controlled_buffer_11
  assign out_7[1] = decoder_1_out3 ? out_8[1] : 1'bz;  // Controlled_Buffer controlled_buffer_12
  assign out_7[0] = decoder_1_out0 ? out_11[0] : 1'bz;  // Controlled_Buffer controlled_buffer_13
  assign out_7[0] = decoder_1_out1 ? out_10[0] : 1'bz;  // Controlled_Buffer controlled_buffer_14
  assign out_7[0] = decoder_1_out2 ? out_9[0] : 1'bz;  // Controlled_Buffer controlled_buffer_15
  assign out_7[0] = decoder_1_out3 ? out_8[0] : 1'bz;  // Controlled_Buffer controlled_buffer_16
  Register #(.width(4)) Register_B (.D(Input_for_Register_B), .en(1'b1), .Q(out_10), .clk(clock_1_out), .clr(in_6));
  Register #(.width(4)) Register_A (.D(Input_for_Register_A), .en(1'b1), .Q(out_11), .clk(clock_1_out), .clr(in_6));

  // Notes on the sheet:
  //   23CS054
endmodule
