// Logisim project circuit 2.circ as structural Verilog: 2 circuits, main circuit main
module main (
  input  in_1,
  input  in_2,
  input  in_3,
  input  in_4
);

  wire circuit_1_1_a2, circuit_1_1_b2, circuit_1_1_c2, circuit_1_1_d2, circuit_1_1_e, circuit_1_1_f,
       circuit_1_1_g;

  circuit_1 circuit_1_1 (
    .a(in_1), .b(in_2), .c(in_3), .d(in_4), .a2(circuit_1_1_a2), .b2(circuit_1_1_b2), .c2(circuit_1_1_c2),
    .d2(circuit_1_1_d2), .e(circuit_1_1_e), .f(circuit_1_1_f), .g(circuit_1_1_g));
  _7_Segment_Display u_7_segment_display_1 (
    .g(circuit_1_1_g), .f(circuit_1_1_f), .a(circuit_1_1_a2), .b(circuit_1_1_b2), .e(circuit_1_1_e),
    .d(circuit_1_1_d2), .c(circuit_1_1_c2));  // open: dp
endmodule

module circuit_1 (
  input  a,
  input  b,
  input  c,
  input  d,
  output a2,
  output b2,
  output c2,
  output d2,
  output e,
  output f,
  output g
);

  wire and_1_out, and_2_out, and_3_out, and_4_out, and_5_out, and_6_out, and_7_out, and_8_out, and_9_out,
       and_10_out, and_11_out, and_12_out, and_13_out, and_14_out, and_15_out, not_1_out, not_2_out,
       not_3_out, not_4_out, not_5_out, not_6_out, not_7_out, not_8_out, not_9_out, not_10_out, not_11_out,
       not_12_out, not_13_out, not_14_out, not_15_out, not_16_out, not_17_out, not_18_out, not_19_out;

  not not_1 (not_1_out, b);
  and and_1 (and_1_out, not_1_out, not_2_out);
  not not_2 (not_2_out, d);
  and and_2 (and_2_out, b, d);
  not not_3 (not_3_out, b);
  not not_4 (not_4_out, c);
  and and_3 (and_3_out, not_4_out, not_5_out);
  not not_5 (not_5_out, d);
  and and_4 (and_4_out, c, d);
  not not_6 (not_6_out, c);
  not not_7 (not_7_out, b);
  and and_5 (and_5_out, not_7_out, not_8_out);
  not not_8 (not_8_out, d);
  not not_9 (not_9_out, b);
  and and_6 (and_6_out, not_9_out, c);
  and and_7 (and_7_out, c, not_10_out);
  not not_10 (not_10_out, d);
  and and_8 (and_8_out, b, not_11_out, d);
  not not_11 (not_11_out, c);
  not not_12 (not_12_out, d);
  and and_9 (and_9_out, a, b);
  not not_13 (not_13_out, c);
  and and_10 (and_10_out, not_13_out, not_14_out);
  not not_14 (not_14_out, d);
  and and_11 (and_11_out, b, not_15_out);
  not not_15 (not_15_out, c);
  and and_12 (and_12_out, b, not_16_out);
  not not_16 (not_16_out, d);
  not not_17 (not_17_out, b);
  and and_13 (and_13_out, not_17_out, c);
  and and_14 (and_14_out, c, not_18_out);
  not not_18 (not_18_out, d);
  and and_15 (and_15_out, b, not_19_out, d);
  not not_19 (not_19_out, c);
  or or_1 (a2, and_1_out, c, and_2_out, a);
  or or_2 (b2, not_3_out, and_3_out, and_4_out, a);
  or or_3 (c2, not_6_out, d, b, a);
  or or_4 (d2, and_5_out, and_6_out, and_7_out, and_8_out, a);
  or or_5 (e, not_12_out, and_9_out);
  or or_6 (f, and_10_out, and_11_out, and_12_out, a);
  or or_7 (g, and_13_out, and_14_out, and_15_out, a);
endmodule
